# Fritzing sketch board_schema_0.1 (saved by Fritzing 0.9.3b)
breadboards: 1

parts:
  Componente1 = Arduino Nano (Rev3.0)
  8_Channel_Relay1 = 8 Channel Power Relay
  0x18 = MCP9808 High Accuracy I2C Temperature Sensor [part_number=.]
  7805 = Voltage Regulator [package=78xxl]
  part = Electrolytic Capacitor [capacitance=10µF package="1010 [SMD, electrolytic]"]
  12V = Power Jack [package=power_jack_slot]
  0x19 = MCP9808 High Accuracy I2C Temperature Sensor [part_number=.]
  0X1A = MCP9808 High Accuracy I2C Temperature Sensor [part_number=.]
  DHT22 = DHT22 Humidity and Temperature Sensor

nets:
  GND: Componente1.RESET, 8_Channel_Relay1.GND, 0x18.GND, 7805.GND, part.-, 12V.GND, 0x19.GND, 0X1A.GND, DHT22.GND
  N1: Componente1.D4, DHT22.DATA
  N2: Componente1.D5, 8_Channel_Relay1.IN8
  N3: Componente1.D6, 8_Channel_Relay1.IN7
  N4: Componente1.D7, 8_Channel_Relay1.IN6
  N5: Componente1.D8, 8_Channel_Relay1.IN5
  N6: Componente1.D9, 8_Channel_Relay1.IN4
  N7: Componente1.D10, 8_Channel_Relay1.IN3
  N8: Componente1.D11/MOSI, 8_Channel_Relay1.IN2
  N9: Componente1.D12/MISO, 8_Channel_Relay1.IN1
  VDD: Componente1.5V, 8_Channel_Relay1.VCC, 0x18.VDD, 0x19.VDD, 0x19.A0, 0X1A.VDD, 0X1A.A1, DHT22.VDD
  N10: Componente1.A5, 0x18.SCL, 0x19.SCL, 0X1A.SCL
  N11: Componente1.A4, 0x18.SDA, 0x19.SDA, 0X1A.SDA
  N12: 8_Channel_Relay1.JD-VCC, 7805.OUT
  N13: 7805.IN, part.+, 12V.PWR

custom parts:
  8 Channel Power Relay: An 8 channel power relay. The module operates at 5V.
  MCP9808 High Accuracy I2C Temperature Sensor: This I2C digital temperature sensor is one of the more accurate/precise we've ever seen, with a typical accuracy of ±0.25°C over the sensor's -40°C to +125°C range and precision of +0.0625°C. They work great with any microcontroller using standard i2c. There are 3 address pins so you can connect up to 8 to a single I2C bus without address collisions. Best of all, a wide voltage range makes is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
